# Fritzing sketch UNO-Dash__Fritzing-Datei (saved by Fritzing 1.0.8)
breadboards: 1

parts:
  U1 = WS2812 RGB LED matrix 8x8
  Bauteil1 = Arduino Uno (Rev3) - ICSP
  S1 = Pushbutton [package="[THT]"]

nets:
  GND: U1.GND, Bauteil1.GND, S1.Pin_1, S1.Pin_2
  VCC: U1.VCC, Bauteil1.5V
  N1: U1.DIN, Bauteil1.D6_PWM
  N2: Bauteil1.D2, S1.Pin_3, S1.Pin_4

custom parts:
  WS2812 RGB LED matrix 8x8: WS2812 matrix 8x8
